// Logisim project 32bit.circ as structural Verilog
module Half_Adder (
  input  A,
  input  B,
  output S,
  output Cout
);

  and and_1 (Cout, B, A);
  xor xor_1 (S, A, B);
endmodule

module Full_Adder (
  input  A,
  input  B,
  input  Cin,
  output S,
  output Cout
);

  wire half_adder_1_cout, half_adder_1_s, half_adder_2_cout;

  Half_Adder half_adder_1 (.A(A), .B(B), .S(half_adder_1_s), .Cout(half_adder_1_cout));
  Half_Adder half_adder_2 (.A(half_adder_1_s), .B(Cin), .S(S), .Cout(half_adder_2_cout));
  or or_1 (Cout, half_adder_2_cout, half_adder_1_cout);
endmodule

module Four_Bit_Adder (
  input  X3,
  input  Y3,
  input  X2,
  input  Y2,
  input  X1,
  input  Y1,
  input  X0,
  input  Y0,
  input  Cin,
  output Cout,
  output S3,
  output S2,
  output S1,
  output S0
);

  wire full_adder_2_cout, full_adder_3_cout, full_adder_4_cout;

  Full_Adder full_adder_1 (.A(X3), .B(Y3), .Cin(full_adder_2_cout), .S(S3), .Cout(Cout));
  Full_Adder full_adder_2 (.A(X2), .B(Y2), .Cin(full_adder_3_cout), .S(S2), .Cout(full_adder_2_cout));
  Full_Adder full_adder_3 (.A(X1), .B(Y1), .Cin(full_adder_4_cout), .S(S1), .Cout(full_adder_3_cout));
  Full_Adder full_adder_4 (.A(X0), .B(Y0), .Cin(Cin), .S(S0), .Cout(full_adder_4_cout));
endmodule

module Sixteen_Bit_Adder (
  input  [3:0] Y3,
  input  [3:0] X3,
  input  [3:0] Y2,
  input  [3:0] X2,
  input  [3:0] Y1,
  input  [3:0] X1,
  input  [3:0] Y0,
  input  [3:0] X0,
  input  Cin,
  output Cout,
  output [3:0] S3,
  output [3:0] S2,
  output [3:0] S1,
  output [3:0] S0
);

  wire four_bit_adder_2_cout, four_bit_adder_3_cout, four_bit_adder_4_cout;

  Four_Bit_Adder four_bit_adder_1 (
    .X3(X3[3]), .Y3(Y3[3]), .X2(X3[2]), .Y2(Y3[2]), .X1(X3[1]), .Y1(Y3[1]), .X0(X3[0]), .Y0(Y3[0]),
    .Cin(four_bit_adder_2_cout), .Cout(Cout), .S3(S3[3]), .S2(S3[2]), .S1(S3[1]), .S0(S3[0]));
  Four_Bit_Adder four_bit_adder_2 (
    .X3(X2[3]), .Y3(Y2[3]), .X2(X2[2]), .Y2(Y2[2]), .X1(X2[1]), .Y1(Y2[1]), .X0(X2[0]), .Y0(Y2[0]),
    .Cin(four_bit_adder_3_cout), .Cout(four_bit_adder_2_cout), .S3(S2[3]), .S2(S2[2]), .S1(S2[1]), .S0(S2[0]));
  Four_Bit_Adder four_bit_adder_3 (
    .X3(X1[3]), .Y3(Y1[3]), .X2(X1[2]), .Y2(Y1[2]), .X1(X1[1]), .Y1(Y1[1]), .X0(X1[0]), .Y0(Y1[0]),
    .Cin(four_bit_adder_4_cout), .Cout(four_bit_adder_3_cout), .S3(S1[3]), .S2(S1[2]), .S1(S1[1]), .S0(S1[0]));
  Four_Bit_Adder four_bit_adder_4 (
    .X3(X0[3]), .Y3(Y0[3]), .X2(X0[2]), .Y2(Y0[2]), .X1(X0[1]), .Y1(Y0[1]), .X0(X0[0]), .Y0(Y0[0]),
    .Cin(Cin), .Cout(four_bit_adder_4_cout), .S3(S0[3]), .S2(S0[2]), .S1(S0[1]), .S0(S0[0]));
  Hex_Digit_Display hex_digit_display_1 (.value(S0));  // open: dp
  Hex_Digit_Display hex_digit_display_2 (.value(S3));  // open: dp
  Hex_Digit_Display hex_digit_display_3 (.value(S2));  // open: dp
  Hex_Digit_Display hex_digit_display_4 (.value(S1));  // open: dp
endmodule

module ThirtyTwo_Bit_Adder (
  input  [7:0] Y3,
  input  [7:0] X3,
  input  [7:0] Y2,
  input  [7:0] X2,
  input  [7:0] Y1,
  input  [7:0] X1,
  input  [7:0] Y0,
  input  [7:0] X0,
  input  Cin,
  output Cout
);

  wire sixteen_bit_adder_2_cout;
  wire [3:0] sixteen_bit_adder_1_s0, sixteen_bit_adder_1_s1, sixteen_bit_adder_1_s2, sixteen_bit_adder_1_s3,
       sixteen_bit_adder_2_s0, sixteen_bit_adder_2_s1, sixteen_bit_adder_2_s2, sixteen_bit_adder_2_s3;

  Sixteen_Bit_Adder sixteen_bit_adder_1 (
    .Y3(Y3[7:4]), .X3(X3[7:4]), .Y2(Y3[3:0]), .X2(X3[3:0]), .Y1(Y2[7:4]), .X1(X2[7:4]), .Y0(Y2[3:0]),
    .X0(X2[3:0]), .Cin(sixteen_bit_adder_2_cout), .Cout(Cout), .S3(sixteen_bit_adder_1_s3),
    .S2(sixteen_bit_adder_1_s2), .S1(sixteen_bit_adder_1_s1), .S0(sixteen_bit_adder_1_s0));
  Sixteen_Bit_Adder sixteen_bit_adder_2 (
    .Y3(Y1[7:4]), .X3(X1[7:4]), .Y2(Y1[3:0]), .X2(X1[3:0]), .Y1(Y0[7:4]), .X1(X0[7:4]), .Y0(Y0[3:0]),
    .X0(X0[3:0]), .Cin(Cin), .Cout(sixteen_bit_adder_2_cout), .S3(sixteen_bit_adder_2_s3),
    .S2(sixteen_bit_adder_2_s2), .S1(sixteen_bit_adder_2_s1), .S0(sixteen_bit_adder_2_s0));
  Hex_Digit_Display hex_digit_display_1 (.value(sixteen_bit_adder_1_s3));  // open: dp
  Hex_Digit_Display hex_digit_display_2 (.value(sixteen_bit_adder_2_s3));  // open: dp
  Hex_Digit_Display hex_digit_display_3 (.value(sixteen_bit_adder_1_s2));  // open: dp
  Hex_Digit_Display hex_digit_display_4 (.value(sixteen_bit_adder_2_s2));  // open: dp
  Hex_Digit_Display hex_digit_display_5 (.value(sixteen_bit_adder_1_s1));  // open: dp
  Hex_Digit_Display hex_digit_display_6 (.value(sixteen_bit_adder_1_s0));  // open: dp
  Hex_Digit_Display hex_digit_display_7 (.value(sixteen_bit_adder_2_s1));  // open: dp
  Hex_Digit_Display hex_digit_display_8 (.value(sixteen_bit_adder_2_s0));  // open: dp
endmodule
