// Logisim project Ask2.circ as structural Verilog: 1 circuit, main circuit main
module main (
  input  A,
  input  B,
  input  C,
  output F
);

  wire and_1_out, and_2_out, and_3_out, and_4_out, not_1_out, not_2_out, not_3_out;

  not not_1 (not_1_out, A);
  not not_2 (not_2_out, B);
  not not_3 (not_3_out, C);
  and and_1 (and_1_out, not_1_out, B, C);
  and and_2 (and_2_out, A, not_2_out, C);
  and and_3 (and_3_out, A, B, not_3_out);
  and and_4 (and_4_out, A, B, C);
  or or_1 (F, and_1_out, and_2_out, and_3_out, and_4_out);

  // Notes on the sheet:
  //   m3=A'*B*C
  //   m5=A*B'*C
  //   m6=A*B*C'
  //   m7=A*B*C
  //   F(A,B,C)=m3+m5+m6+m7=(A'*B*C)+(A*B'*C)+(A*B*C')+(A*B*C)
endmodule
