// Logisim project Comp4x4.circ as structural Verilog
module Comparator_1x1 (
  input  A0,
  input  B0,
  output A0_L_B0,
  output A0_E_B0,
  output A0_G_B0
);

  wire not_1_out, not_2_out;

  not not_1 (not_1_out, A0);
  not not_2 (not_2_out, B0);
  and and_1 (A0_L_B0, not_1_out, B0);
  and and_2 (A0_G_B0, A0, not_2_out);
  nor nor_1 (A0_E_B0, A0_L_B0, A0_G_B0);
endmodule

module Comparator_2x2 (
  input  A1,
  input  B1,
  input  A0,
  input  B0,
  output A_L_B,
  output A_E_B,
  output A_G_B
);

  wire and_1_out, and_2_out, comparator_1x1_1_a0_e_b0, comparator_1x1_1_a0_g_b0, comparator_1x1_1_a0_l_b0,
       comparator_1x1_2_a0_e_b0, comparator_1x1_2_a0_g_b0, comparator_1x1_2_a0_l_b0;

  Comparator_1x1 comparator_1x1_1 (
    .A0(A1), .B0(B1), .A0_L_B0(comparator_1x1_1_a0_l_b0), .A0_E_B0(comparator_1x1_1_a0_e_b0),
    .A0_G_B0(comparator_1x1_1_a0_g_b0));
  Comparator_1x1 comparator_1x1_2 (
    .A0(A0), .B0(B0), .A0_L_B0(comparator_1x1_2_a0_l_b0), .A0_E_B0(comparator_1x1_2_a0_e_b0),
    .A0_G_B0(comparator_1x1_2_a0_g_b0));
  and and_1 (and_1_out, comparator_1x1_1_a0_e_b0, comparator_1x1_2_a0_l_b0);
  and and_2 (and_2_out, comparator_1x1_2_a0_g_b0, comparator_1x1_1_a0_e_b0);
  or or_1 (A_L_B, comparator_1x1_1_a0_l_b0, and_1_out);
  and and_3 (A_E_B, comparator_1x1_1_a0_e_b0, comparator_1x1_2_a0_e_b0);
  or or_2 (A_G_B, comparator_1x1_1_a0_g_b0, and_2_out);
endmodule

module Comparator_4x4 (
  input  [3:0] A,
  input  [3:0] B,
  output A_L_B,
  output A_E_B,
  output A_G_B
);

  wire and_2_out, and_3_out, comparator_2x2_1_a_e_b, comparator_2x2_1_a_g_b, comparator_2x2_1_a_l_b,
       comparator_2x2_2_a_e_b, comparator_2x2_2_a_g_b, comparator_2x2_2_a_l_b;

  Comparator_2x2 comparator_2x2_1 (
    .A1(A[3]), .B1(B[3]), .A0(A[2]), .B0(B[2]), .A_L_B(comparator_2x2_1_a_l_b),
    .A_E_B(comparator_2x2_1_a_e_b), .A_G_B(comparator_2x2_1_a_g_b));
  Comparator_2x2 comparator_2x2_2 (
    .A1(A[1]), .B1(B[1]), .A0(A[0]), .B0(B[0]), .A_L_B(comparator_2x2_2_a_l_b),
    .A_E_B(comparator_2x2_2_a_e_b), .A_G_B(comparator_2x2_2_a_g_b));
  and and_1 (A_E_B, comparator_2x2_1_a_e_b, comparator_2x2_2_a_e_b);
  and and_2 (and_2_out, comparator_2x2_1_a_e_b, comparator_2x2_2_a_l_b);
  and and_3 (and_3_out, comparator_2x2_2_a_g_b, comparator_2x2_1_a_e_b);
  or or_1 (A_L_B, comparator_2x2_1_a_l_b, and_2_out);
  or or_2 (A_G_B, comparator_2x2_1_a_g_b, and_3_out);
endmodule
