// Logisim project MUX_2x1.circ as structural Verilog
module MUX2x1 (
  input  [7:0] S,
  input  [7:0] D0,
  input  [7:0] D1,
  input  [7:0] E,
  output [7:0] Y
);

  wire [7:0] and_1_out, and_2_out, not_1_out, not_2_out;

  assign not_1_out = ~S;  // NOT_Gate not_1, 8 bits wide
  assign not_2_out = ~E;  // NOT_Gate not_2, 8 bits wide
  assign and_1_out = D0 & not_2_out & not_1_out;  // AND_Gate and_1, 8 bits wide
  assign and_2_out = D1 & not_2_out & S;  // AND_Gate and_2, 8 bits wide
  assign Y = and_1_out | and_2_out;  // OR_Gate or_1, 8 bits wide
endmodule
