// Logisim project dec4x16.circ as structural Verilog
module dec_4x16 (
  input  [3:0] A,
  output D1,
  output D2,
  output D0,
  output D4,
  output D3,
  output D5,
  output D6,
  output D7,
  output D9,
  output D8,
  output D10,
  output D11,
  output D12,
  output D13,
  output D14,
  output D15
);

  wire not_1_out;

  not not_1 (not_1_out, A[3]);
  Decoder #(.select(3)) decoder_1 (
    .out0(D0), .out1(D1), .out2(D2), .out3(D3), .out4(D4), .out5(D5), .out6(D6), .out7(D7), .sel(A[2:0]),
    .en(not_1_out));
  Decoder #(.select(3)) decoder_2 (
    .out0(D8), .out1(D9), .out2(D10), .out3(D11), .out4(D12), .out5(D13), .out6(D14), .out7(D15),
    .sel(A[2:0]), .en(A[3]));
endmodule
