// Logisim project Counter4bit.circ as structural Verilog
module Counter_4bit (
  output A0,
  output A1,
  output A2,
  output A3
);

  wire Clear_out, CLK_out, PresetA0_out, PresetA1_out, PresetA2_out, PresetA3_out,
       Qa_OR_Qb_AND_Qc_AND_Qd_out, Qb_AND_Qc_AND_Qd_out, Qc_AND_Qd_out, t_ff_4_qn;

  Button Clear (.out(Clear_out));
  and Qc_AND_Qd (Qc_AND_Qd_out, A0, A1);
  and Qb_AND_Qc_AND_Qd (Qb_AND_Qc_AND_Qd_out, Qc_AND_Qd_out, A2);
  or Qa_OR_Qb_AND_Qc_AND_Qd (Qa_OR_Qb_AND_Qc_AND_Qd_out, Qb_AND_Qc_AND_Qd_out, A3);
  Clock CLK (.out(CLK_out));
  Button PresetA0 (.out(PresetA0_out));
  T_Flip_Flop #(.trigger("falling")) t_ff_1 (
    .T(t_ff_4_qn), .clk(CLK_out), .Q(A0), .reset(Clear_out), .preset(PresetA0_out));  // open: Qn
  Button PresetA1 (.out(PresetA1_out));
  T_Flip_Flop #(.trigger("falling")) t_ff_2 (
    .T(A0), .clk(CLK_out), .Q(A1), .reset(Clear_out), .preset(PresetA1_out));  // open: Qn
  Button PresetA2 (.out(PresetA2_out));
  T_Flip_Flop #(.trigger("falling")) t_ff_3 (
    .T(Qc_AND_Qd_out), .clk(CLK_out), .Q(A2), .reset(Clear_out), .preset(PresetA2_out));  // open: Qn
  T_Flip_Flop #(.trigger("falling")) t_ff_4 (
    .T(Qa_OR_Qb_AND_Qc_AND_Qd_out), .clk(CLK_out), .Q(A3), .Qn(t_ff_4_qn), .reset(Clear_out),
    .preset(PresetA3_out));
  Button PresetA3 (.out(PresetA3_out));

  // Notes on the sheet:
  //   Td
  //   Qd
  //   Tc
  //   Qc
  //   Tb
  //   Qb
  //   Ta
  //   Qa
  //   Qa'
endmodule
