// Logisim project alu.circ as structural Verilog
module ALU (
  input  [3:0] A,
  input  [3:0] B,
  input  [2:0] S,
  output [3:0] Outpt,
  output Cout
);

  wire adder_1_cout, adder_2_cout;
  wire [3:0] A_AND_B_out, adder_1_out, adder_2_out, NOT_A_out, NOT_B_out;

  assign NOT_A_out = ~A;  // NOT_Gate NOT_A, 4 bits wide
  assign NOT_B_out = ~B;  // NOT_Gate NOT_B, 4 bits wide
  Adder #(.width(4)) adder_1 (.a(A), .b(B), .out(adder_1_out), .cout(adder_1_cout));  // open: cin
  Adder #(.width(4)) adder_2 (.a(B), .b(4'b0001), .out(adder_2_out), .cout(adder_2_cout));  // open: cin
  assign A_AND_B_out = A & B;  // AND_Gate A_AND_B, 4 bits wide
  Multiplexer #(.select(3)) multiplexer_1 (
    .in2(adder_1_cout), .in4(adder_2_cout), .out(Cout), .sel(S));  // open: in0, in1, in3, in5, in6, in7
  Multiplexer #(.select(3), .width(4)) multiplexer_2 (
    .in0(NOT_A_out), .in1(NOT_B_out), .in2(adder_1_out), .in3(A_AND_B_out), .in4(adder_2_out), .out(Outpt),
    .sel(S));  // open: in5, in6, in7

  // Notes on the sheet:
  //   A+B
  //   B+1
endmodule
